# Fritzing sketch demo (saved by Fritzing 0.9.3b)
circuit board: 8.46667cm x 5.64444cm
breadboards: 2

parts:
  U1 = ESP32-38PinWide [part_number=ESP32-38PinWide]
  Grove1 = Grove OLED 128x96
  J1 = Basic Servo

nets:
  N1: U1.3.3, Grove1.VCC
  GND: U1.GND, Grove1.GND, J1.gnd
  VIN: U1.VIN, J1.vcc
  N2: U1.GPIO16, J1.pulse
  N3: U1.GPIO21, Grove1.SCL
  N4: U1.GPIO22, Grove1.SDA

custom parts:
  ESP32-38PinWide: Generic 38-Pin ESP32 with wide format (only access to one side of pins on a breadboard) based on Stephen Lilley's HiLetgo ESP-WROOM-32 ESP32 ESP-32S Development Board.
